# Fritzing sketch Circuit Breadboard (saved by Fritzing 0.9.3b)
breadboards: 1

parts:
  OLED_I2C1 = OLED 128x64 I2C Monochrome Display
  Part1 = Blackberry Trackballer Breakout
  Part2 = Photon
  Part3 = Mini Lipo  # not connected
  Part4 = Lithium Ion Polymer Battery 3.7v 350mAh [part_number=2750]  # not connected

nets:
  N1: OLED_I2C1.SDA, Part2.D0
  N2: OLED_I2C1.SCK, Part2.D1
  VDD: OLED_I2C1.VDD, Part1.VCC, Part2.3V3
  GND: OLED_I2C1.GND, Part1.GND, Part2.GND
  N3: Part1.BTN, Part2.D2
  N4: Part1.BLU, Part2.D5
  N5: Part1.RED, Part2.A4
  N6: Part1.WHT, Part2.D3
  N7: Part1.UP, Part2.D6
  N8: Part1.DWN, Part2.D7

custom parts:
  Mini Lipo: Oh so handy, this little lipo charger is so small and easy to use you can keep it on your desk or mount it easily into any project! Simply plug it via any MiniUSB cable into a USB port and a 3.7V/4.2V lithium polymer or lithium ion rechargeable battery into the JST plug on the other end. There are two LEDs - one red and one green. While charging, the red LED is lit. When the battery is fully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
  Lithium Ion Polymer Battery 3.7v 350mAh: Lithium ion polymer (also known as 'lipo' or 'lipoly') batteries are thin, light and powerful. The output ranges from 4.2V when completely charged to 3.7V. This battery has a capacity of 350mAh for a total of about 1.3 Wh. The batteries come pre-attached with a genuine 2-pin JST-PH connector as shown and include the necessary protection circuitry.
