# Fritzing sketch Circuit Schematic (saved by Fritzing 0.9.3b)

parts:
  Part1 = Photon
  Part2 = Blackberry Trackballer Breakout
  Part4 = Mini Lipo
  Part5 = Lithium Ion Polymer Battery 3.7v 350mAh [part_number=2750]
  Squix2 = OLED 0.96" 128x64 I2C SSD1306

nets:
  N1: Part1.A4, Part2.RED
  GND: Part1.GND, Part2.GND, Part4.GND, Part5.negative, Squix2.GND
  VIN: Part1.VIN, Part4.5V, Part5.positive
  N2: Part1.D0, Squix2.SCA
  N3: Part1.D1, Squix2.SCL
  N4: Part1.D2, Part2.BTN
  N5: Part1.D3, Part2.WHT
  N6: Part1.D5, Part2.BLU
  N7: Part1.D6, Part2.UP
  N8: Part1.D7, Part2.DWN
  VCC: Part1.3V3, Part2.VCC, Squix2.VCC

custom parts:
  Mini Lipo: Oh so handy, this little lipo charger is so small and easy to use you can keep it on your desk or mount it easily into any project! Simply plug it via any MiniUSB cable into a USB port and a 3.7V/4.2V lithium polymer or lithium ion rechargeable battery into the JST plug on the other end. There are two LEDs - one red and one green. While charging, the red LED is lit. When the battery is fully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
  Lithium Ion Polymer Battery 3.7v 350mAh: Lithium ion polymer (also known as 'lipo' or 'lipoly') batteries are thin, light and powerful. The output ranges from 4.2V when completely charged to 3.7V. This battery has a capacity of 350mAh for a total of about 1.3 Wh. The batteries come pre-attached with a genuine 2-pin JST-PH connector as shown and include the necessary protection circuitry.
